# Fritzing sketch Papel (saved by Fritzing 0.9.4)

parts:
  Mod1 = Digispark
  R2 = Resistor [tolerance=±5% resistance=470k package=THT]
  R3 = Resistor [tolerance=±5% resistance=100k package=THT]
  J1 = Piezo Speaker
  TRS1 = Audio Jack (TRS) 3.5mm [package="4Ucon 08780 [THT]"]
  R4 = Photocell (LDR) [package=THT]

nets:
  N1: Mod1.VCC, R4.pin_1
  N2: Mod1.GND, R2.Pin_0, R3.Pin_0, J1.pin1, TRS1.Sleeve
  N3: R3.Pin_1, R4.pin_0
  N4: J1.pin2, TRS1.Tip

notes:
  SUPERFICIE DE CONTACTO
  (FRECUENCIA)
  LDR
  (TIEMPO DE DISPARO)

custom parts:
  Digispark: The Digispark is an Attiny85 based microcontroller development board similar to the Arduino line, only cheaper, smaller, and a bit less powerful. With a whole host of shields to extend its functionality and the ability to use the familiar Arduino IDE the Digispark is a great way to jump into electronics, or perfect for when an Arduino is too big or too much. May 2019 modified to correct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
